# Fritzing sketch air-quality (saved by Fritzing 0.9.3b)
breadboards: 1

parts:
  U1 = NodeMCU V1.0
  Bauteil2 = Adafruit CCS811

nets:
  N1: U1.D1, Bauteil2.SCL
  N2: U1.D2, Bauteil2.SDA
  3V3: U1.3V3, Bauteil2.3.3V, Bauteil2.!WAKE
  GND: U1.GND, Bauteil2.GND

custom parts:
  NodeMCU V1.0: ESP8266 based NodeMCU
